# Fritzing sketch myProject (saved by Fritzing 0.9.3b)
breadboards: 1

parts:
  VCC1 = 4 x AAA Battery Mount
  M1 = DC Motor
  M2 = DC Motor
  Parça1 = Arduino Uno (Rev3)
  hc-sr1 = hc-sr04
  S1 = H-Bridge with L298N
  J1 = Piezo Speaker
  Parça2 = Bluetooth HC-05 Macho

nets:
  N1: VCC1.-, S1.GND
  N2: VCC1.+, S1.12V
  N3: M1.pin_1, S1.M1-02
  N4: M1.pin_2, S1.M1-01
  N5: M2.pin_1, S1.M2-02
  N6: M2.pin_2, S1.M2-01
  N7: Parça1.A0, hc-sr1.Echo
  N8: Parça1.A1, hc-sr1.Trig
  N9: Parça1.D8, J1.pin2
  N10: Parça1.D9_PWM, Parça2.TXD
  N11: Parça1.D10_PWM/SS, Parça2.RXD
  N12: Parça1.D11_PWM/MOSI, S1.IN3
  N13: Parça1.D12/MISO, S1.IN4
  N14: Parça1.D13/SCK, S1.ENB
  GND: Parça1.GND, hc-sr1.GND, Parça2.GND
  N15: Parça1.D3_PWM, S1.ENA
  N16: Parça1.D4, S1.IN1
  N17: Parça1.D5_PWM, S1.IN2
  5V: Parça1.5V, hc-sr1.VCC

custom parts:
  H-Bridge with L298N: h-bridge
